# Fritzing sketch Breadboard Layout (saved by Fritzing 0.7.1b)
breadboards: 1

parts:
  LED1 = LED - 5mm [color="Red (633nm)" package="5 mm [THT]"]
  LED2 = LED - 5mm [color="Red (633nm)" package="5 mm [THT]"]
  LED3 = LED - 5mm [color="Red (633nm)" package="5 mm [THT]"]
  LED4 = LED - 5mm [color="Red (633nm)" package="5 mm [THT]"]
  LED5 = LED - 5mm [color="Red (633nm)" package="5 mm [THT]"]
  LED6 = LED - 5mm [color="Red (633nm)" package="5 mm [THT]"]
  LED7 = LED - 5mm [color="Red (633nm)" package="5 mm [THT]"]
  LED8 = LED - 5mm [color="Red (633nm)" package="5 mm [THT]"]
  LED9 = LED - 5mm [color="Red (633nm)" package="5 mm [THT]"]
  LED10 = LED - 5mm [color="Red (633nm)" package="5 mm [THT]"]
  LED11 = LED - 5mm [color="Red (633nm)" package="5 mm [THT]"]
  LED12 = LED - 5mm [color="Red (633nm)" package="5 mm [THT]"]
  LED13 = LED - 5mm [color="Red (633nm)" package="5 mm [THT]"]
  LED14 = LED - 5mm [color="Red (633nm)" package="5 mm [THT]"]
  LED15 = LED - 5mm [color="Red (633nm)" package="5 mm [THT]"]
  LED16 = LED - 5mm [color="Red (633nm)" package="5 mm [THT]"]
  LED17 = LED - 5mm [color="Red (633nm)" package="5 mm [THT]"]
  LED18 = LED - 5mm [color="Red (633nm)" package="5 mm [THT]"]
  LED19 = LED - 5mm [color="Red (633nm)" package="5 mm [THT]"]
  LED20 = LED - 5mm [color="Red (633nm)" package="5 mm [THT]"]
  R1 = Resistor [tolerance=±5% resistance=220 package=THT]
  R2 = Resistor [tolerance=±5% resistance=220 package=THT]
  R3 = Resistor [tolerance=±5% resistance=220 package=THT]
  R4 = Resistor [tolerance=±5% resistance=220 package=THT]
  R5 = Resistor [tolerance=±5% resistance=220 package=THT]
  Arduino1 = Arduino

nets:
  N1: LED1.cathode, LED2.cathode, LED3.cathode, LED4.cathode, LED8.anode, LED12.anode, LED16.anode, LED20.anode, R1.Pin_1
  N2: LED1.anode, LED5.anode, LED9.anode, LED13.anode, LED17.cathode, LED18.cathode, LED19.cathode, LED20.cathode, R5.Pin_1
  N3: LED2.anode, LED6.anode, LED10.anode, LED13.cathode, LED14.cathode, LED15.cathode, LED16.cathode, LED17.anode, R4.Pin_1
  N4: LED3.anode, LED7.anode, LED9.cathode, LED10.cathode, LED11.cathode, LED12.cathode, LED14.anode, LED18.anode, R3.Pin_1
  N5: LED4.anode, LED5.cathode, LED6.cathode, LED7.cathode, LED8.cathode, LED11.anode, LED15.anode, LED19.anode, R2.Pin_1
  N6: R1.Pin_0, Arduino1.D2
  N7: R2.Pin_0, Arduino1.D3
  N8: R3.Pin_0, Arduino1.D4
  N9: R4.Pin_0, Arduino1.D5
  N10: R5.Pin_0, Arduino1.D6
